# Fritzing sketch tictactino (saved by Fritzing 0.7.12b)
breadboards: 1

parts:
  U2 = 74HC595 [package="DIP16 [THT]"]
  U3 = 74HC595 [package="DIP16 [THT]"]
  S1 = Pushbutton [package="[THT]"]
  S2 = Pushbutton [package="[THT]"]
  Arduino1 = Arduino
  U4 = 74HC595 [package="DIP16 [THT]"]
  J1 = Generic female header - 9 pins [package=THT]
  J2 = Generic female header - 9 pins [package=THT]
  J3 = Generic female header - 4 pins [package=THT]
  R1 = Resistor [tolerance=±5% resistance=150 package=THT]
  R2 = Resistor [tolerance=±5% resistance=150 package=THT]
  R3 = Resistor [tolerance=±5% resistance=150 package=THT]
  R4 = Resistor [tolerance=±5% resistance=150 package=THT]
  R5 = Resistor [tolerance=±5% resistance=150 package=THT]
  R6 = Resistor [tolerance=±5% resistance=150 package=THT]
  R7 = Resistor [tolerance=±5% resistance=150 package=THT]
  R8 = Resistor [tolerance=±5% resistance=150 package=THT]
  R9 = Resistor [tolerance=±5% resistance=150 package=THT]
  R10 = Resistor [tolerance=±5% resistance=150 package=THT]
  R11 = Resistor [tolerance=±5% resistance=150 package=THT]
  R12 = Resistor [tolerance=±5% resistance=150 package=THT]
  R13 = Resistor [tolerance=±5% resistance=150 package=THT]
  R14 = Resistor [tolerance=±5% resistance=150 package=THT]
  R15 = Resistor [tolerance=±5% resistance=150 package=THT]
  R16 = Resistor [tolerance=±5% resistance=150 package=THT]
  R17 = Resistor [tolerance=±5% resistance=150 package=THT]
  R18 = Resistor [tolerance=±5% resistance=150 package=THT]
  J4 = Generic female header - 2 pins [package=THT]
  R19 = Resistor [tolerance=±5% resistance=10k package=THT]
  R20 = Resistor [tolerance=±5% resistance=10k package=THT]

nets (from the schematic view):
  N1: U2.Q1, R10.Pin_0
  N2: U2.Q2, R15.Pin_0
  N3: U2.Q3, R16.Pin_0
  N4: U2.Q4, R13.Pin_0
  N5: U2.Q5, R12.Pin_0
  N6: U2.Q6, R11.Pin_0
  N7: U2.Q7, R18.Pin_0
  GND: U2.GND, U2.OE, U3.GND, U3.OE, Arduino1.GND, U4.GND, U4.OE, R19.Pin_1, R20.Pin_1
  N8: U2.Q7', U3.DS
  VCC: U2.MR, U2.VCC, U3.MR, U3.VCC, S1.Pin_3, S1.Pin_4, S2.Pin_3, S2.Pin_4, Arduino1.+5V, U4.MR, U4.VCC
  N9: U2.SH_CP, U3.SH_CP, Arduino1.D4, U4.SH_CP
  N10: U2.ST_CP, U3.ST_CP, Arduino1.D3, U4.ST_CP
  N11: U2.DS, U4.Q7'
  N12: U2.Q0, R9.Pin_0
  N13: U3.Q1, R17.Pin_0
  N14: U3.Q2, J3.pin4
  N15: U3.Q3, J3.pin3
  N16: U3.Q4, J3.pin2
  N17: U3.Q5, J3.pin1
  N18: U3.Q6, J4.pin2
  N19: U3.Q7, J4.pin1
  N20: U3.Q0, R14.Pin_0
  N21: S1.Pin_1, S1.Pin_2, Arduino1.D6, R19.Pin_0
  N22: S2.Pin_1, S2.Pin_2, Arduino1.D7, R20.Pin_0
  N23: Arduino1.D5, U4.DS
  N24: U4.Q1, R2.Pin_0
  N25: U4.Q2, R3.Pin_0
  N26: U4.Q3, R4.Pin_0
  N27: U4.Q4, R5.Pin_0
  N28: U4.Q5, R6.Pin_0
  N29: U4.Q6, R7.Pin_0
  N30: U4.Q7, R8.Pin_0
  N31: U4.Q0, R1.Pin_0
  N32: J1.pin1, R9.Pin_1
  N33: J1.pin2, R8.Pin_1
  N34: J1.pin3, R7.Pin_1
  N35: J1.pin4, R6.Pin_1
  N36: J1.pin5, R5.Pin_1
  N37: J1.pin6, R4.Pin_1
  N38: J1.pin7, R3.Pin_1
  N39: J1.pin8, R2.Pin_1
  N40: J1.pin9, R1.Pin_1
  N41: J2.pin1, R17.Pin_1
  N42: J2.pin2, R14.Pin_1
  N43: J2.pin3, R18.Pin_1
  N44: J2.pin4, R11.Pin_1
  N45: J2.pin5, R12.Pin_1
  N46: J2.pin6, R13.Pin_1
  N47: J2.pin7, R16.Pin_1
  N48: J2.pin8, R15.Pin_1
  N49: J2.pin9, R10.Pin_1

notes:
  LEDs gruen Anode
  LEDs rot Anode
  Zaehler
  frei
  LEDs grün Anode
  unbenutzt
  LEDs sind nicht eingezeichnet.
  9 x bicolor LED mit gem. Kathode
  4 Bit Spielzug-Zähler;
  kann opt. für 7 Segment
  Anzeige genutz werden;
  Weitere 2 Bit zur freien Verwendung

custom parts:
  74HC595: 8-bit parallel-load shift registers
